// Logisim project ROM_Microcontroller.circ as structural Verilog: 1 circuit, main circuit main
// Trans_End
module main (
);

  wire and_1_out, and_2_out, and_4_out, and_5_out, and_6_out, Change_State, clock_1_out, d_ff_2_q, d_ff_5_q,
       Done, Enter_Enb, Exit_Enb, or_1_out, or_2_out, or_3_out, or_5_out, Point, Restart, Routine_End, RST,
       Run, Select_Next, Store, User_Enb;
  wire [1:1] Control_data;
  wire [3:0] bit_extender_1_out, bit_extender_2_out;
  wire [4:0] Pointer_q;
  wire [5:0] Curr_State, History_Stack_dout, multiplexer_1_out, Next_State, Routine_q;
  wire [7:0] Comb_Inputs, Func_Inputs, Func_Outputs;
  wire [8:0] Enter_Func_data, Exit_Func_data, Outputs, User_Func_data;
  wire [13:0] register_1_q;

  Button button_1 (.out(RST));
  Register #(.trigger("low"), .width(14)) register_1 (
    .D({Comb_Inputs, Curr_State}), .Q(register_1_q), .clk(Run), .clr(RST));  // open: en
  DipSwitch dipswitch_1 (
    .sw1(Comb_Inputs[7]), .sw2(Comb_Inputs[6]), .sw3(Comb_Inputs[5]), .sw4(Comb_Inputs[4]),
    .sw5(Comb_Inputs[3]), .sw6(Comb_Inputs[2]), .sw7(Comb_Inputs[1]), .sw8(Comb_Inputs[0]));
  Counter #(.max('h1f), .width(5)) Pointer (
    .Q(Pointer_q), .up(Select_Next), .clk(Point), .clr(RST));  // open: load, D, count, carry
  DipSwitch dipswitch_2 (
    .sw1(Func_Inputs[7]), .sw2(Func_Inputs[6]), .sw3(Func_Inputs[5]), .sw4(Func_Inputs[4]),
    .sw5(Func_Inputs[3]), .sw6(Func_Inputs[2]), .sw7(Func_Inputs[1]), .sw8(Func_Inputs[0]));
  RAM #(.addrWidth(5), .dataWidth(6), .enables("line")) History_Stack (
    .addr(Pointer_q), .we(Store), .clk(Store), .din(Curr_State), .dout(History_Stack_dout));
  ROM #(.addrWidth(16), .dataWidth(9)) Combin (.addr({2'b00, register_1_q}), .data(Outputs));
  ROM #(.addrWidth(16), .dataWidth(9)) Control (
    .addr({1'b0, Routine_End, register_1_q}), .data({Next_State, Select_Next, Control_data[1], Run}));
  Multiplexer #(.width(6)) multiplexer_1 (
    .in0(History_Stack_dout), .in1(Next_State), .out(multiplexer_1_out), .sel(Select_Next));
  and and_1 (and_1_out, or_5_out, and_2_out);
  Register #(.width(6)) State_ID (.D(multiplexer_1_out), .Q(Curr_State), .clk(Change_State), .clr(RST));  // open: en
  Counter #(.max('h3f), .width(6)) Routine (
    .count(or_1_out), .Q(Routine_q), .clk(clock_1_out), .clr(or_2_out));  // open: load, D, carry, up
  or or_1 (or_1_out, and_1_out, User_Enb);
  or or_2 (or_2_out, Restart, RST);
  Clock clock_1 (.out(clock_1_out));
  and and_2 (and_2_out, Run, ~Control_data[1]);  // AND_Gate
  and and_3 (User_Enb, Run, Control_data[1]);
  and and_4 (and_4_out, clock_1_out, and_2_out, Done);
  Bit_Extender #(.out_width(4)) bit_extender_1 (.in(Func_Inputs), .out(bit_extender_1_out));
  Bit_Extender #(.out_width(4)) bit_extender_2 (.in(Func_Inputs), .out(bit_extender_2_out));
  or or_3 (or_3_out, Routine_End, RST);
  ROM #(.addrWidth(16), .dataWidth(9)) User_Func (
    .addr({bit_extender_1_out, Curr_State, Routine_q}), .data(User_Func_data));
  ROM #(.addrWidth(16), .dataWidth(9)) Enter_Func (
    .addr({bit_extender_2_out, Curr_State, Routine_q}), .data(Enter_Func_data));
  ROM #(.addrWidth(16), .dataWidth(9)) Exit_Func (
    .addr({bit_extender_2_out, Curr_State, Routine_q}), .data(Exit_Func_data));
  D_Flip_Flop d_ff_1 (.D(d_ff_5_q), .clk(and_4_out), .Q(Exit_Enb), .preset(or_3_out));  // open: Qn, reset
  D_Flip_Flop d_ff_2 (.D(Exit_Enb), .clk(and_4_out), .Q(d_ff_2_q), .reset(or_3_out));  // open: Qn, preset
  D_Flip_Flop d_ff_3 (.D(d_ff_2_q), .clk(and_4_out), .Q(Change_State), .reset(or_3_out));  // open: Qn, preset
  D_Flip_Flop d_ff_4 (.D(Change_State), .clk(and_4_out), .Q(Enter_Enb), .reset(or_3_out));  // open: Qn, preset
  D_Flip_Flop d_ff_5 (.D(Enter_Enb), .clk(and_4_out), .Q(d_ff_5_q), .reset(or_3_out));  // open: Qn, preset
  or or_4 (Point, and_5_out, and_6_out);
  and and_5 (and_5_out, Select_Next, Change_State);
  and and_6 (and_6_out, ~Select_Next, d_ff_2_q);  // AND_Gate
  and and_7 (Store, Select_Next, d_ff_2_q);
  assign Func_Outputs = User_Enb ? User_Func_data[8:1] : 8'bz;  // Controlled_Buffer controlled_buffer_1
  assign Func_Outputs = Enter_Enb ? Enter_Func_data[8:1] : 8'bz;  // Controlled_Buffer controlled_buffer_2
  assign Func_Outputs = Exit_Enb ? Exit_Func_data[8:1] : 8'bz;  // Controlled_Buffer controlled_buffer_3
  Pull_Resistor pull_resistor_1 (.node(Func_Outputs));
  or or_5 (or_5_out, Exit_Enb, Enter_Enb);
  or or_6 (Done, Enter_Func_data[0], Exit_Func_data[0]);
  or or_7 (Restart, Exit_Enb, Enter_Enb);
  or or_8 (Routine_End, d_ff_5_q, User_Func_data[0]);
endmodule
